// Logisim project 2013182010 김병진 Logisim(2X1MUX...8Bit_Shifter).circ as structural Verilog
module _2X1_MUX (
  input  Select,
  input  I0,
  input  I1,
  output O
);

  wire and_1_out, and_2_out, not_1_out;

  not not_1 (not_1_out, Select);
  and and_1 (and_1_out, not_1_out, I0);
  and and_2 (and_2_out, Select, I1);
  or or_1 (O, and_1_out, and_2_out);
endmodule

module _4X1_MUX (
  input  S1,
  input  S0,
  input  I0,
  input  I1,
  input  I2,
  input  I3,
  output O
);

  wire and_1_out, and_2_out, and_3_out, and_4_out, not_1_out, not_2_out;

  not not_1 (not_1_out, S1);
  not not_2 (not_2_out, S0);
  and and_1 (and_1_out, not_2_out, not_1_out, I0);
  and and_2 (and_2_out, S0, not_1_out, I1);
  and and_3 (and_3_out, not_2_out, S1, I2);
  and and_4 (and_4_out, S0, S1, I3);
  or or_1 (O, and_1_out, and_2_out, and_3_out, and_4_out);
endmodule

// 1LU
module _1Bit_LU (
  input  A,
  input  B,
  input  S1,
  input  S0,
  output out_5
);

  wire and_1_out, not_1_out, or_1_out, xor_1_out;

  and and_1 (and_1_out, A, B);
  or or_1 (or_1_out, A, B);
  xor xor_1 (xor_1_out, A, B);
  not not_1 (not_1_out, A);
  _4X1_MUX u_4x1_mux_1 (.S1(S1), .S0(S0), .I0(and_1_out), .I1(or_1_out), .I2(xor_1_out), .I3(not_1_out), .O(out_5));
endmodule

// 4bit LU
module _4Bit_LU (
  input  [3:0] A,
  input  [3:0] B,
  input  S1,
  input  S0,
  output [3:0] F
);

  _1Bit_LU u_1bit_lu_1 (.A(A[0]), .B(B[0]), .S1(S1), .S0(S0), .out_5(F[0]));
  _1Bit_LU u_1bit_lu_2 (.A(A[1]), .B(B[1]), .S1(S1), .S0(S0), .out_5(F[1]));
  _1Bit_LU u_1bit_lu_3 (.A(A[2]), .B(B[2]), .S1(S1), .S0(S0), .out_5(F[2]));
  _1Bit_LU u_1bit_lu_4 (.A(A[3]), .B(B[3]), .S1(S1), .S0(S0), .out_5(F[3]));
endmodule

module _4Bit_Shifter (
  input  SLin,
  input  [3:0] I,
  input  SRin,
  input  S1,
  input  S0,
  output [3:0] O
);

  _4X1_MUX u_4x1_mux_1 (.S1(S1), .S0(S0), .I0(I[0]), .I1(I[1]), .I2(SLin), .I3(1'b0), .O(O[0]));
  _4X1_MUX u_4x1_mux_2 (.S1(S1), .S0(S0), .I0(I[1]), .I1(I[2]), .I2(I[0]), .I3(1'b0), .O(O[1]));
  _4X1_MUX u_4x1_mux_3 (.S1(S1), .S0(S0), .I0(I[2]), .I1(I[3]), .I2(I[1]), .I3(1'b0), .O(O[2]));
  _4X1_MUX u_4x1_mux_4 (.S1(S1), .S0(S0), .I0(I[3]), .I1(SRin), .I2(I[2]), .I3(1'b0), .O(O[3]));
endmodule

module _8Bit_LU (
  input  [7:0] in_1,
  input  [7:0] in_2,
  input  S1,
  input  S0,
  output [7:0] out_5
);

  _4Bit_LU u_4bit_lu_1 (.A(in_1[3:0]), .B(in_2[3:0]), .S1(S1), .S0(S0), .F(out_5[3:0]));
  _4Bit_LU u_4bit_lu_2 (.A(in_1[7:4]), .B(in_2[7:4]), .S1(S1), .S0(S0), .F(out_5[7:4]));
endmodule

module _8Bit_Shifter (
  input  SLin,
  input  [7:0] I,
  input  SRin,
  input  S1,
  input  S0,
  output [7:0] O
);

  wire and_1_out, and_2_out, or_1_out, or_2_out;

  and and_1 (and_1_out, I[3], S1);
  and and_2 (and_2_out, S0, I[4]);
  or or_1 (or_1_out, SLin, and_1_out);
  or or_2 (or_2_out, SRin, and_2_out);
  _4Bit_Shifter u_4bit_shifter_1 (.SLin(SLin), .I(I[3:0]), .SRin(or_2_out), .S1(S1), .S0(S0), .O(O[3:0]));
  _4Bit_Shifter u_4bit_shifter_2 (.SLin(or_1_out), .I(I[7:4]), .SRin(SRin), .S1(S1), .S0(S0), .O(O[7:4]));
endmodule

module _8Bit_Pistol (
  input  [7:0] in_1,
  input  S1,
  input  S0,
  input  [7:0] in_4,
  output [7:0] out_5
);

  _4Bit_LU u_4bit_lu_1 (.A(in_1[3:0]), .B(in_4[3:0]), .S1(S0), .S0(S1), .F(out_5[7:4]));
  _4Bit_LU u_4bit_lu_2 (.A(in_1[7:4]), .B(in_4[7:4]), .S1(S0), .S0(S1), .F(out_5[3:0]));
endmodule
