// Logisim project 2013182010 김병진 Logisim(4bit 2X1MUX...8Bit_ALU).circ as structural Verilog
module _2X1_MUX (
  input  Select,
  input  I0,
  input  I1,
  output O
);

  wire and_1_out, and_2_out, not_1_out;

  not not_1 (not_1_out, Select);
  and and_1 (and_1_out, not_1_out, I0);
  and and_2 (and_2_out, Select, I1);
  or or_1 (O, and_1_out, and_2_out);
endmodule

module _4X1_MUX (
  input  S1,
  input  S0,
  input  I0,
  input  I1,
  input  I2,
  input  I3,
  output O
);

  wire and_1_out, and_2_out, and_3_out, and_4_out, not_1_out, not_2_out;

  not not_1 (not_1_out, S1);
  not not_2 (not_2_out, S0);
  and and_1 (and_1_out, not_2_out, not_1_out, I0);
  and and_2 (and_2_out, S0, not_1_out, I1);
  and and_3 (and_3_out, not_2_out, S1, I2);
  and and_4 (and_4_out, S0, S1, I3);
  or or_1 (O, and_1_out, and_2_out, and_3_out, and_4_out);
endmodule

// 1LU
module _1Bit_LU (
  input  A,
  input  B,
  input  S1,
  input  S0,
  output out_5
);

  wire and_1_out, not_1_out, or_1_out, xor_1_out;

  and and_1 (and_1_out, A, B);
  or or_1 (or_1_out, A, B);
  xor xor_1 (xor_1_out, A, B);
  not not_1 (not_1_out, A);
  _4X1_MUX u_4x1_mux_1 (.S1(S1), .S0(S0), .I0(and_1_out), .I1(or_1_out), .I2(xor_1_out), .I3(not_1_out), .O(out_5));
endmodule

// 4LU
module _4Bit_LU (
  input  [3:0] A,
  input  [3:0] B,
  input  S1,
  input  S0,
  output [3:0] F
);

  _1Bit_LU u_1bit_lu_1 (.A(A[0]), .B(B[0]), .S1(S1), .S0(S0), .out_5(F[0]));
  _1Bit_LU u_1bit_lu_2 (.A(A[1]), .B(B[1]), .S1(S1), .S0(S0), .out_5(F[1]));
  _1Bit_LU u_1bit_lu_3 (.A(A[2]), .B(B[2]), .S1(S1), .S0(S0), .out_5(F[2]));
  _1Bit_LU u_1bit_lu_4 (.A(A[3]), .B(B[3]), .S1(S1), .S0(S0), .out_5(F[3]));
endmodule

module _4Bit_Shifter (
  input  SLin,
  input  [3:0] I,
  input  SRin,
  input  S1,
  input  S0,
  output [3:0] O
);

  _4X1_MUX u_4x1_mux_1 (.S1(S1), .S0(S0), .I0(I[0]), .I1(I[1]), .I2(SLin), .I3(1'b0), .O(O[0]));
  _4X1_MUX u_4x1_mux_2 (.S1(S1), .S0(S0), .I0(I[1]), .I1(I[2]), .I2(I[0]), .I3(1'b0), .O(O[1]));
  _4X1_MUX u_4x1_mux_3 (.S1(S1), .S0(S0), .I0(I[2]), .I1(I[3]), .I2(I[1]), .I3(1'b0), .O(O[2]));
  _4X1_MUX u_4x1_mux_4 (.S1(S1), .S0(S0), .I0(I[3]), .I1(SRin), .I2(I[2]), .I3(1'b0), .O(O[3]));
endmodule

// 8LU
module _8Bit_LU (
  input  [7:0] in_1,
  input  [7:0] in_2,
  input  S1,
  input  S0,
  output [7:0] out_5
);

  _4Bit_LU u_4bit_lu_1 (.A(in_1[3:0]), .B(in_2[3:0]), .S1(S1), .S0(S0), .F(out_5[3:0]));
  _4Bit_LU u_4bit_lu_2 (.A(in_1[7:4]), .B(in_2[7:4]), .S1(S1), .S0(S0), .F(out_5[7:4]));
endmodule

// 8SH
module _8Bit_Shifter (
  input  SLin,
  input  [7:0] I,
  input  SRin,
  input  S1,
  input  S0,
  output [7:0] O
);

  wire and_1_out, and_2_out, or_1_out, or_2_out;

  and and_1 (and_1_out, I[3], S1);
  and and_2 (and_2_out, S0, I[4]);
  or or_1 (or_1_out, SLin, and_1_out);
  or or_2 (or_2_out, SRin, and_2_out);
  _4Bit_Shifter u_4bit_shifter_1 (.SLin(SLin), .I(I[3:0]), .SRin(or_2_out), .S1(S1), .S0(S0), .O(O[3:0]));
  _4Bit_Shifter u_4bit_shifter_2 (.SLin(or_1_out), .I(I[7:4]), .SRin(SRin), .S1(S1), .S0(S0), .O(O[7:4]));
endmodule

// FA
module Full_Adder (
  input  A,
  input  B,
  input  Ci,
  output S,
  output Co
);

  wire and_1_out, and_2_out, and_3_out, and_4_out, and_5_out, and_6_out, and_7_out, not_1_out, not_2_out,
       not_3_out, not_4_out, not_5_out, not_6_out;

  not not_1 (not_1_out, A);
  not not_2 (not_2_out, B);
  not not_3 (not_3_out, A);
  not not_4 (not_4_out, Ci);
  not not_5 (not_5_out, B);
  not not_6 (not_6_out, Ci);
  and and_1 (and_1_out, B, Ci);
  and and_2 (and_2_out, A, Ci);
  and and_3 (and_3_out, A, B);
  and and_4 (and_4_out, not_1_out, not_2_out, Ci);
  and and_5 (and_5_out, not_3_out, B, not_4_out);
  and and_6 (and_6_out, A, not_5_out, not_6_out);
  and and_7 (and_7_out, A, B, Ci);
  or or_1 (Co, and_1_out, and_2_out, and_3_out);
  or or_2 (S, and_4_out, and_5_out, and_6_out, and_7_out);
endmodule

// 1 AU
module _1Bit_AU (
  input  Carry_in,
  input  A,
  input  B,
  input  S1,
  input  S0,
  output F,
  output Carry_Out
);

  wire n4x1_mux_1_o, not_1_out;

  not not_1 (not_1_out, B);
  _4X1_MUX u_4x1_mux_1 (.S1(S1), .S0(S0), .I0(1'b0), .I1(B), .I2(not_1_out), .I3(1'b1), .O(n4x1_mux_1_o));
  Full_Adder full_adder_1 (.A(A), .B(n4x1_mux_1_o), .Ci(Carry_in), .S(F), .Co(Carry_Out));
endmodule

// 4 AU
module _4Bit_AU (
  input  Carry_in,
  input  [3:0] A,
  input  [3:0] B,
  input  S1,
  input  S0,
  output [3:0] F,
  output LastBit_Carry_Out,
  output oVerflow,
  output Carryout
);

  wire n1bit_au_1_carry_out, n1bit_au_2_carry_out;

  _1Bit_AU u_1bit_au_1 (
    .Carry_in(Carry_in), .A(A[0]), .B(B[0]), .S1(S1), .S0(S0), .F(F[0]), .Carry_Out(n1bit_au_1_carry_out));
  _1Bit_AU u_1bit_au_2 (
    .Carry_in(n1bit_au_1_carry_out), .A(A[1]), .B(B[1]), .S1(S1), .S0(S0), .F(F[1]),
    .Carry_Out(n1bit_au_2_carry_out));
  _1Bit_AU u_1bit_au_3 (
    .Carry_in(n1bit_au_2_carry_out), .A(A[2]), .B(B[2]), .S1(S1), .S0(S0), .F(F[2]),
    .Carry_Out(LastBit_Carry_Out));
  _1Bit_AU u_1bit_au_4 (
    .Carry_in(LastBit_Carry_Out), .A(A[3]), .B(B[3]), .S1(S1), .S0(S0), .F(F[3]), .Carry_Out(Carryout));
  xor xor_1 (oVerflow, LastBit_Carry_Out, Carryout);
endmodule

// 8AU
module _8Bit_AU (
  input  Carry_in,
  input  [7:0] A,
  input  [7:0] B,
  input  S1,
  input  S0,
  output [7:0] F,
  output oVerflow,
  output Cary_Out
);

  wire n4bit_au_1_carryout, n4bit_au_2_lastbit_carry_out;

  _4Bit_AU u_4bit_au_1 (
    .Carry_in(Carry_in), .A(A[3:0]), .B(B[3:0]), .S1(S1), .S0(S0), .F(F[3:0]), .Carryout(n4bit_au_1_carryout));  // open: oVerflow, LastBit_Carry_Out
  _4Bit_AU u_4bit_au_2 (
    .Carry_in(n4bit_au_1_carryout), .A(A[7:4]), .B(B[7:4]), .S1(S1), .S0(S0), .F(F[7:4]),
    .Carryout(Cary_Out), .LastBit_Carry_Out(n4bit_au_2_lastbit_carry_out));  // open: oVerflow
  xor xor_1 (oVerflow, n4bit_au_2_lastbit_carry_out, Cary_Out);
endmodule

// 4 2X1
module _4Bit_2X1_MUX (
  input  [3:0] A,
  input  [3:0] B,
  input  S0,
  output [3:0] O
);

  _2X1_MUX u_2x1_mux_1 (.Select(S0), .I0(A[0]), .I1(B[0]), .O(O[0]));
  _2X1_MUX u_2x1_mux_2 (.Select(S0), .I0(A[1]), .I1(B[1]), .O(O[1]));
  _2X1_MUX u_2x1_mux_3 (.Select(S0), .I0(A[2]), .I1(B[2]), .O(O[2]));
  _2X1_MUX u_2x1_mux_4 (.Select(S0), .I0(A[3]), .I1(B[3]), .O(O[3]));
endmodule

// 8 2X1
module _8Bit_2X1_MUX (
  input  [7:0] A,
  input  [7:0] B,
  input  S0,
  output [7:0] O
);

  _4Bit_2X1_MUX u_4bit_2x1_mux_1 (.A(A[3:0]), .B(B[3:0]), .S0(S0), .O(O[3:0]));
  _4Bit_2X1_MUX u_4bit_2x1_mux_2 (.A(A[7:4]), .B(B[7:4]), .S0(S0), .O(O[7:4]));
endmodule

module _4Bit_ALU (
  input  [3:0] A,
  input  [3:0] B,
  input  S2,
  input  H1,
  input  S1,
  input  S0,
  input  H0,
  input  Ci,
  output oVerflow,
  output Carry_Out,
  output Z,
  output Sign,
  output [3:0] F
);

  wire [3:0] n4bit_2x1_mux_1_o, n4bit_au_1_f, n4bit_lu_1_f;

  _4Bit_LU u_4bit_lu_1 (.A(A), .B(B), .S1(S1), .S0(S0), .F(n4bit_lu_1_f));
  _4Bit_AU u_4bit_au_1 (
    .Carry_in(Ci), .A(A), .B(B), .S1(S1), .S0(S0), .F(n4bit_au_1_f), .oVerflow(oVerflow), .Carryout(Carry_Out));  // open: LastBit_Carry_Out
  _4Bit_2X1_MUX u_4bit_2x1_mux_1 (.A(n4bit_au_1_f), .B(n4bit_lu_1_f), .S0(S2), .O(n4bit_2x1_mux_1_o));
  _4Bit_Shifter u_4bit_shifter_1 (.SLin(1'b0), .I(n4bit_2x1_mux_1_o), .SRin(1'b0), .S1(H1), .S0(H0), .O(F));
  nor nor_1 (Z, F[0], F[1], F[2], F[3]);

  assign Sign = F[3];
endmodule

module _8Bit_ALU (
  input  [7:0] A,
  input  [7:0] B,
  input  S2,
  input  S1,
  input  S0,
  input  Carry_in,
  input  H1,
  input  H0,
  output oVerflow,
  output Carry_Out,
  output Z,
  output S,
  output [7:0] F
);

  wire [7:0] n8bit_2x1_mux_1_o, n8bit_au_1_f, n8bit_lu_1_out_5;

  _8Bit_AU u_8bit_au_1 (
    .Carry_in(Carry_in), .A(A), .B(B), .S1(S1), .S0(S0), .F(n8bit_au_1_f), .oVerflow(oVerflow),
    .Cary_Out(Carry_Out));
  _8Bit_LU u_8bit_lu_1 (.in_1(A), .in_2(B), .S1(S1), .S0(S0), .out_5(n8bit_lu_1_out_5));
  _8Bit_2X1_MUX u_8bit_2x1_mux_1 (.A(n8bit_au_1_f), .B(n8bit_lu_1_out_5), .S0(S2), .O(n8bit_2x1_mux_1_o));
  _8Bit_Shifter u_8bit_shifter_1 (.SLin(1'b0), .I(n8bit_2x1_mux_1_o), .SRin(1'b0), .S1(H1), .S0(H0), .O(F));
  nor nor_1 (Z, F[0], F[1], F[2], F[3], F[4], F[5], F[6], F[7]);

  assign S = F[7];
endmodule
