// Logisim project 2013182010 김병진 Logisim(CPU_Final).circ as structural Verilog
module _2X1_MUX (
  input  Select,
  input  I0,
  input  I1,
  output O
);

  wire and_1_out, and_2_out, not_1_out;

  not not_1 (not_1_out, Select);
  and and_1 (and_1_out, not_1_out, I0);
  and and_2 (and_2_out, Select, I1);
  or or_1 (O, and_1_out, and_2_out);
endmodule

module _4X1_MUX (
  input  S1,
  input  S0,
  input  I0,
  input  I1,
  input  I2,
  input  I3,
  output O
);

  wire and_1_out, and_2_out, and_3_out, and_4_out, not_1_out, not_2_out;

  not not_1 (not_1_out, S1);
  not not_2 (not_2_out, S0);
  and and_1 (and_1_out, not_2_out, not_1_out, I0);
  and and_2 (and_2_out, S0, not_1_out, I1);
  and and_3 (and_3_out, not_2_out, S1, I2);
  and and_4 (and_4_out, S0, S1, I3);
  or or_1 (O, and_1_out, and_2_out, and_3_out, and_4_out);
endmodule

// 1LU
module _1Bit_LU (
  input  A,
  input  B,
  input  S1,
  input  S0,
  output out_5
);

  wire and_1_out, not_1_out, or_1_out, xor_1_out;

  and and_1 (and_1_out, A, B);
  or or_1 (or_1_out, A, B);
  xor xor_1 (xor_1_out, A, B);
  not not_1 (not_1_out, A);
  _4X1_MUX u_4x1_mux_1 (.S1(S1), .S0(S0), .I0(and_1_out), .I1(or_1_out), .I2(xor_1_out), .I3(not_1_out), .O(out_5));
endmodule

// 4LU
module _4Bit_LU (
  input  [3:0] A,
  input  [3:0] B,
  input  S1,
  input  S0,
  output [3:0] F
);

  _1Bit_LU u_1bit_lu_1 (.A(A[0]), .B(B[0]), .S1(S1), .S0(S0), .out_5(F[0]));
  _1Bit_LU u_1bit_lu_2 (.A(A[1]), .B(B[1]), .S1(S1), .S0(S0), .out_5(F[1]));
  _1Bit_LU u_1bit_lu_3 (.A(A[2]), .B(B[2]), .S1(S1), .S0(S0), .out_5(F[2]));
  _1Bit_LU u_1bit_lu_4 (.A(A[3]), .B(B[3]), .S1(S1), .S0(S0), .out_5(F[3]));
endmodule

module _4Bit_Shifter (
  input  SLin,
  input  [3:0] I,
  input  SRin,
  input  S1,
  input  S0,
  output [3:0] O
);

  _4X1_MUX u_4x1_mux_1 (.S1(S1), .S0(S0), .I0(I[0]), .I1(I[1]), .I2(SLin), .I3(1'b0), .O(O[0]));
  _4X1_MUX u_4x1_mux_2 (.S1(S1), .S0(S0), .I0(I[1]), .I1(I[2]), .I2(I[0]), .I3(1'b0), .O(O[1]));
  _4X1_MUX u_4x1_mux_3 (.S1(S1), .S0(S0), .I0(I[2]), .I1(I[3]), .I2(I[1]), .I3(1'b0), .O(O[2]));
  _4X1_MUX u_4x1_mux_4 (.S1(S1), .S0(S0), .I0(I[3]), .I1(SRin), .I2(I[2]), .I3(1'b0), .O(O[3]));
endmodule

// 8LU
module _8Bit_LU (
  input  [7:0] in_1,
  input  [7:0] in_2,
  input  S1,
  input  S0,
  output [7:0] out_5
);

  _4Bit_LU u_4bit_lu_1 (.A(in_1[3:0]), .B(in_2[3:0]), .S1(S1), .S0(S0), .F(out_5[3:0]));
  _4Bit_LU u_4bit_lu_2 (.A(in_1[7:4]), .B(in_2[7:4]), .S1(S1), .S0(S0), .F(out_5[7:4]));
endmodule

// 8SH
module _8Bit_Shifter (
  input  SLin,
  input  [7:0] I,
  input  SRin,
  input  S1,
  input  S0,
  output [7:0] O
);

  wire and_1_out, and_2_out, or_1_out, or_2_out;

  and and_1 (and_1_out, I[3], S1);
  and and_2 (and_2_out, S0, I[4]);
  or or_1 (or_1_out, SLin, and_1_out);
  or or_2 (or_2_out, SRin, and_2_out);
  _4Bit_Shifter u_4bit_shifter_1 (.SLin(SLin), .I(I[3:0]), .SRin(or_2_out), .S1(S1), .S0(S0), .O(O[3:0]));
  _4Bit_Shifter u_4bit_shifter_2 (.SLin(or_1_out), .I(I[7:4]), .SRin(SRin), .S1(S1), .S0(S0), .O(O[7:4]));
endmodule

// FA
module Full_Adder (
  input  A,
  input  B,
  input  Ci,
  output S,
  output Co
);

  wire and_1_out, and_2_out, and_3_out, and_4_out, and_5_out, and_6_out, and_7_out, not_1_out, not_2_out,
       not_3_out, not_4_out, not_5_out, not_6_out;

  not not_1 (not_1_out, A);
  not not_2 (not_2_out, B);
  not not_3 (not_3_out, A);
  not not_4 (not_4_out, Ci);
  not not_5 (not_5_out, B);
  not not_6 (not_6_out, Ci);
  and and_1 (and_1_out, B, Ci);
  and and_2 (and_2_out, A, Ci);
  and and_3 (and_3_out, A, B);
  and and_4 (and_4_out, not_1_out, not_2_out, Ci);
  and and_5 (and_5_out, not_3_out, B, not_4_out);
  and and_6 (and_6_out, A, not_5_out, not_6_out);
  and and_7 (and_7_out, A, B, Ci);
  or or_1 (Co, and_1_out, and_2_out, and_3_out);
  or or_2 (S, and_4_out, and_5_out, and_6_out, and_7_out);
endmodule

// 1 AU
module _1Bit_AU (
  input  Carry_in,
  input  A,
  input  B,
  input  S1,
  input  S0,
  output F,
  output Carry_Out
);

  wire n4x1_mux_1_o, not_1_out;

  not not_1 (not_1_out, B);
  _4X1_MUX u_4x1_mux_1 (.S1(S1), .S0(S0), .I0(1'b0), .I1(B), .I2(not_1_out), .I3(1'b1), .O(n4x1_mux_1_o));
  Full_Adder full_adder_1 (.A(A), .B(n4x1_mux_1_o), .Ci(Carry_in), .S(F), .Co(Carry_Out));
endmodule

// 4 AU
module _4Bit_AU (
  input  Carry_in,
  input  [3:0] A,
  input  [3:0] B,
  input  S1,
  input  S0,
  output [3:0] F,
  output LastBit_Carry_Out,
  output oVerflow,
  output Carryout
);

  wire n1bit_au_1_carry_out, n1bit_au_2_carry_out;

  _1Bit_AU u_1bit_au_1 (
    .Carry_in(Carry_in), .A(A[0]), .B(B[0]), .S1(S1), .S0(S0), .F(F[0]), .Carry_Out(n1bit_au_1_carry_out));
  _1Bit_AU u_1bit_au_2 (
    .Carry_in(n1bit_au_1_carry_out), .A(A[1]), .B(B[1]), .S1(S1), .S0(S0), .F(F[1]),
    .Carry_Out(n1bit_au_2_carry_out));
  _1Bit_AU u_1bit_au_3 (
    .Carry_in(n1bit_au_2_carry_out), .A(A[2]), .B(B[2]), .S1(S1), .S0(S0), .F(F[2]),
    .Carry_Out(LastBit_Carry_Out));
  _1Bit_AU u_1bit_au_4 (
    .Carry_in(LastBit_Carry_Out), .A(A[3]), .B(B[3]), .S1(S1), .S0(S0), .F(F[3]), .Carry_Out(Carryout));
  xor xor_1 (oVerflow, LastBit_Carry_Out, Carryout);
endmodule

// 8AU
module _8Bit_AU (
  input  Carry_in,
  input  [7:0] A,
  input  [7:0] B,
  input  S1,
  input  S0,
  output [7:0] F,
  output oVerflow,
  output Cary_Out
);

  wire n4bit_au_1_carryout, n4bit_au_2_lastbit_carry_out;

  _4Bit_AU u_4bit_au_1 (
    .Carry_in(Carry_in), .A(A[3:0]), .B(B[3:0]), .S1(S1), .S0(S0), .F(F[3:0]), .Carryout(n4bit_au_1_carryout));  // open: oVerflow, LastBit_Carry_Out
  _4Bit_AU u_4bit_au_2 (
    .Carry_in(n4bit_au_1_carryout), .A(A[7:4]), .B(B[7:4]), .S1(S1), .S0(S0), .F(F[7:4]),
    .Carryout(Cary_Out), .LastBit_Carry_Out(n4bit_au_2_lastbit_carry_out));  // open: oVerflow
  xor xor_1 (oVerflow, n4bit_au_2_lastbit_carry_out, Cary_Out);
endmodule

// 4 2X1
module _4Bit_2X1_MUX (
  input  [3:0] A,
  input  [3:0] B,
  input  S0,
  output [3:0] O
);

  _2X1_MUX u_2x1_mux_1 (.Select(S0), .I0(A[0]), .I1(B[0]), .O(O[0]));
  _2X1_MUX u_2x1_mux_2 (.Select(S0), .I0(A[1]), .I1(B[1]), .O(O[1]));
  _2X1_MUX u_2x1_mux_3 (.Select(S0), .I0(A[2]), .I1(B[2]), .O(O[2]));
  _2X1_MUX u_2x1_mux_4 (.Select(S0), .I0(A[3]), .I1(B[3]), .O(O[3]));
endmodule

// 8 2X1
module _8Bit_2X1_MUX (
  input  [7:0] A,
  input  [7:0] B,
  input  S0,
  output [7:0] O
);

  _4Bit_2X1_MUX u_4bit_2x1_mux_1 (.A(A[3:0]), .B(B[3:0]), .S0(S0), .O(O[3:0]));
  _4Bit_2X1_MUX u_4bit_2x1_mux_2 (.A(A[7:4]), .B(B[7:4]), .S0(S0), .O(O[7:4]));
endmodule

module _4Bit_ALU (
  input  [3:0] A,
  input  [3:0] B,
  input  S2,
  input  H1,
  input  S1,
  input  S0,
  input  H0,
  input  Ci,
  output oVerflow,
  output Carry_Out,
  output Z,
  output Sign,
  output [3:0] F
);

  wire [3:0] n4bit_2x1_mux_1_o, n4bit_au_1_f, n4bit_lu_1_f;

  _4Bit_LU u_4bit_lu_1 (.A(A), .B(B), .S1(S1), .S0(S0), .F(n4bit_lu_1_f));
  _4Bit_AU u_4bit_au_1 (
    .Carry_in(Ci), .A(A), .B(B), .S1(S1), .S0(S0), .F(n4bit_au_1_f), .oVerflow(oVerflow), .Carryout(Carry_Out));  // open: LastBit_Carry_Out
  _4Bit_2X1_MUX u_4bit_2x1_mux_1 (.A(n4bit_au_1_f), .B(n4bit_lu_1_f), .S0(S2), .O(n4bit_2x1_mux_1_o));
  _4Bit_Shifter u_4bit_shifter_1 (.SLin(1'b0), .I(n4bit_2x1_mux_1_o), .SRin(1'b0), .S1(H1), .S0(H0), .O(F));
  nor nor_1 (Z, F[0], F[1], F[2], F[3]);

  assign Sign = F[3];
endmodule

// 8ALU
module _8Bit_ALU (
  input  [7:0] A,
  input  [7:0] B,
  input  [5:0] in_3,
  output oVerflow,
  output Carry_Out,
  output Z,
  output S,
  output [7:0] F
);

  wire [7:0] n8bit_2x1_mux_1_o, n8bit_au_1_f, n8bit_lu_1_out_5;

  _8Bit_AU u_8bit_au_1 (
    .Carry_in(in_3[2]), .A(A), .B(B), .S1(in_3[4]), .S0(in_3[3]), .F(n8bit_au_1_f), .oVerflow(oVerflow),
    .Cary_Out(Carry_Out));
  _8Bit_LU u_8bit_lu_1 (.in_1(A), .in_2(B), .S1(in_3[4]), .S0(in_3[3]), .out_5(n8bit_lu_1_out_5));
  _8Bit_2X1_MUX u_8bit_2x1_mux_1 (.A(n8bit_au_1_f), .B(n8bit_lu_1_out_5), .S0(in_3[5]), .O(n8bit_2x1_mux_1_o));
  _8Bit_Shifter u_8bit_shifter_1 (.SLin(1'b0), .I(n8bit_2x1_mux_1_o), .SRin(1'b0), .S1(in_3[1]), .S0(in_3[0]), .O(F));
  nor nor_1 (Z, F[0], F[1], F[2], F[3], F[4], F[5], F[6], F[7]);

  assign S = F[7];
endmodule

module Control_Bit (
  input  in_1,
  input  in_2,
  input  in_3,
  input  in_4,
  input  in_5,
  input  in_6,
  input  in_7,
  input  in_8,
  output out_9,
  output out_10,
  output out_11
);

  wire acid, clock_1_out, iraddrid, iropid, M, marid, mbrid, not_1_out, pcid, rw, stid;
  wire [1:0] A, B;
  wire [2:0] control_unit_1_count;
  wire [3:0] n8bit_alu_1_overflow, Status_q;
  wire [5:0] ALU;
  wire [7:0] AC_q, controlled_buffer_2_out, IR_Addr_q, IR_OP_q, MAR_q, MBR_q, multiplexer_1_out,
       multiplexer_2_out, multiplexer_3_out, n8bit_alu_1_f, PC_q;

  Multiplexer #(.width(8), .enable("false")) multiplexer_1 (
    .in0(n8bit_alu_1_f), .in1(controlled_buffer_2_out), .out(multiplexer_1_out), .sel(M));
  assign out_11 = in_8 ? in_7 : 1'bz;  // Controlled_Buffer controlled_buffer_1
  Register AC (.D(n8bit_alu_1_f), .en(acid), .Q(AC_q), .clk(clock_1_out), .clr(in_1));
  Register PC (.D(n8bit_alu_1_f), .en(pcid), .Q(PC_q), .clk(clock_1_out), .clr(in_1));
  Register IR_Addr (.D(n8bit_alu_1_f), .en(iraddrid), .Q(IR_Addr_q), .clk(clock_1_out), .clr(in_1));
  Register MBR (.D(multiplexer_1_out), .en(mbrid), .Q(MBR_q), .clk(clock_1_out), .clr(in_1));
  Register MAR (.D(n8bit_alu_1_f), .en(marid), .Q(MAR_q), .clk(clock_1_out), .clr(in_1));
  Clock clock_1 (.out(clock_1_out));
  assign out_9 = in_5 ? ~in_3 : 1'bz;  // Controlled_Inverter controlled_inverter_1
  // Probe on multiplexer_2_out
  Multiplexer #(.select(2), .width(8), .enable("false")) multiplexer_2 (
    .in0(AC_q), .in1(PC_q), .in2(IR_Addr_q), .in3(MBR_q), .out(multiplexer_2_out), .sel(A));
  // Probe on multiplexer_3_out
  Multiplexer #(.select(2), .width(8), .enable("false")) multiplexer_3 (
    .in0(AC_q), .in1(PC_q), .in2(IR_Addr_q), .in3(MBR_q), .out(multiplexer_3_out), .sel(B));
  Register IR_OP (.D(MBR_q), .en(iropid), .Q(IR_OP_q), .clk(clock_1_out), .clr(in_1));
  assign controlled_buffer_2_out = not_1_out ? MBR_q : 8'bz;  // Controlled_Buffer controlled_buffer_2
  not not_1 (not_1_out, rw);
  _8Bit_ALU u_8bit_alu_1 (
    .A(multiplexer_2_out), .B(multiplexer_3_out), .in_3(ALU), .oVerflow(n8bit_alu_1_overflow[0]),
    .Carry_Out(n8bit_alu_1_overflow[1]), .Z(n8bit_alu_1_overflow[2]), .S(n8bit_alu_1_overflow[3]),
    .F(n8bit_alu_1_f));
  // Probe on n8bit_alu_1_f
  Register #(.width(4)) Status (.D(n8bit_alu_1_overflow), .en(stid), .Q(Status_q), .clk(clock_1_out), .clr(in_1));
  xor xor_1 (out_10, in_4, in_6);
  // Probe on control_unit_1_count
  Control_Unit control_unit_1 (
    .Ck(clock_1_out), .Reset(in_1), .State(Status_q), .IR_Op(IR_OP_q), .r_w(rw), .A_MUX(A), .B_MUX(B),
    .Count(control_unit_1_count), .M(M), .ALU(ALU), .LDs({acid, pcid, iraddrid, mbrid, marid, iropid, stid}));
  RAM ram_1 (.addr(MAR_q), .data(controlled_buffer_2_out), .sel(in_2), .clk(clock_1_out), .ld(rw), .clr(in_1));
endmodule

// C U
module Control_Unit (
  input  Ck,
  input  Reset,
  input  [3:0] State,
  input  [7:0] IR_Op,
  output [1:0] A_MUX,
  output [2:0] Count,
  output [1:0] B_MUX,
  output M,
  output r_w,
  output [5:0] ALU,
  output [6:0] LDs
);

  wire AC2BR, ADD, ADD_T4, ADD_T5, ADD_T6, AND, and_19_out, and_20_out, AND_T4, AND_T5, AND_T6, BNZ, BNZ_T4,
       BR2AC, BZ, BZ_T4, IRAD2AR, IRAD2PC, JMP, JMP_T4, LDA, LDA_T4, LDA_T5, NOP, NOT, not_1_out, not_2_out,
       NOT_T4, OR, or_15_out, OR_T4, OR_T5, OR_T6, READ, SHL, SHR, STR, STR_T4, STR_T6, SUB, SUB_T4, SUB_T5,
       SUB_T6, T0, T1, T4, T5, T6, T7, XOR, XOR_T4, XOR_T5;

  and and_1 (LDA_T4, LDA, T4);
  and and_2 (LDA_T5, LDA, T5);
  and and_3 (BR2AC, LDA, T6);
  and and_4 (ADD_T4, ADD, T4);
  and and_5 (ADD_T5, ADD, T5);
  and and_6 (ADD_T6, ADD, T6);
  and and_7 (SUB_T4, SUB, T4);
  and and_8 (SUB_T5, SUB, T5);
  and and_9 (SUB_T6, SUB, T6);
  and and_10 (AND_T4, AND, T4);
  and and_11 (AND_T5, AND, T5);
  and and_12 (AND_T6, AND, T6);
  and and_13 (OR_T4, OR, T4);
  and and_14 (OR_T5, OR, T5);
  and and_15 (OR_T6, OR, T6);
  Counter #(.width(3), .max('h7)) counter_1 (.Q(Count), .clk(not_1_out), .clr(Reset));  // open: load, D, count, carry
  not not_1 (not_1_out, Ck);
  not not_2 (not_2_out, State[2]);
  and and_16 (XOR_T4, XOR, T4);
  and and_17 (XOR_T5, XOR, T5);
  and and_18 (OR_T6, XOR, T6);
  Decoder #(.select(4), .enable("false")) decoder_1 (
    .out0(NOP), .out1(NOT), .out2(SHL), .out3(SHR), .out4(JMP), .out5(BZ), .out6(BNZ), .out8(LDA),
    .out9(ADD), .out10(SUB), .out11(AND), .out12(OR), .out13(XOR), .out15(STR), .sel(IR_Op[7:4]));  // open: out7, out14
  and and_19 (and_19_out, BNZ_T4, not_2_out);
  or or_1 (IRAD2PC, and_19_out, JMP_T4, and_20_out);
  and and_20 (and_20_out, BZ_T4, State[2]);
  and and_21 (NOT_T4, NOT, T4);
  and and_22 (ALU[1], SHL, T4);
  and and_23 (ALU[0], SHR, T4);
  Decoder #(.select(3), .enable("false")) decoder_2 (
    .out0(T0), .out1(T1), .out2(LDs[1]), .out3(LDs[4]), .out4(T4), .out5(T5), .out6(T6), .out7(T7),
    .sel(Count));
  and and_24 (JMP_T4, JMP, T4);
  and and_25 (STR_T4, STR, T4);
  and and_26 (AC2BR, STR, T5);
  and and_27 (STR_T6, STR, T6);
  or or_2 (M, T1, READ, LDs[1]);
  not not_3 (r_w, STR_T6);
  or or_3 (READ, SUB_T5, XOR_T5, OR_T5, AND_T5, ADD_T5, LDA_T5);
  or or_4 (IRAD2AR, LDA_T4, ADD_T4, SUB_T4, AND_T4, OR_T4, XOR_T4, STR_T4);
  and and_28 (BZ_T4, BZ, T4);
  and and_29 (BNZ_T4, BNZ, T4);
  or or_5 (ALU[3], ADD_T6, OR_T6, NOT_T4);
  or or_6 (ALU[4], SUB_T6, OR_T6, NOT_T4);
  or or_7 (A_MUX[0], T0, T1, LDs[1], LDs[4], BR2AC);
  or or_8 (A_MUX[1], LDs[4], IRAD2AR, IRAD2PC, BR2AC);
  or or_9 (B_MUX[1], ADD_T6, SUB_T6, AND_T6, OR_T6, OR_T6);
  or or_10 (ALU[2], T1, SUB_T6, LDs[1]);
  or or_11 (ALU[5], NOT_T4, AND_T6, OR_T6, OR_T6);
  or or_12 (LDs[3], T1, READ, AC2BR, LDs[1]);
  or or_13 (LDs[2], T0, IRAD2AR, T1);
  or or_14 (LDs[5], T1, IRAD2PC, LDs[1]);
  or or_15 (or_15_out, NOT_T4, ALU[1], ALU[0]);
  or or_16 (LDs[6], BR2AC, ADD_T6, SUB_T6, or_15_out, AND_T6, OR_T6, OR_T6);

  assign B_MUX[0] = B_MUX[1];
  assign LDs[0] = LDs[6];

  // Other names for the same wires on the sheet: SHR_T4 = ALU[0]; uSHR = ALU[0]; SHL_T4 = ALU[1]; uSHL = ALU[1];
  //   LDA_T6 = BR2AC; T2 = LDs[1]; T3 = LDs[4]; V = State[0]; C = State[1]; Z = State[2]; S = State[3];
  //   STR_T5 = AC2BR; uADD = ADD_T6; uAND = AND_T6; uNOT = NOT_T4; uSUB = SUB_T6; uOR = OR_T6; uXOR = OR_T6;
  //   XOR_T6 = OR_T6; WRITE = STR_T6
endmodule
