// Logisim project 2013182010 김병진 Logisim(De_morgan...4bit_adder).circ as structural Verilog
module De_Morgan (
  input  in_1,
  input  in_2,
  input  in_3,
  input  in_4,
  output out_5,
  output out_6
);

  wire and_1_out, not_1_out, not_2_out;

  not not_1 (not_1_out, in_3);
  not not_2 (not_2_out, in_4);
  and and_1 (and_1_out, in_1, in_2);
  or or_1 (out_6, not_1_out, not_2_out);
  not not_3 (out_5, and_1_out);
endmodule

// HA
module Half_adder (
  input  A,
  input  B,
  output S,
  output C
);

  xor xor_1 (S, A, B);
  and and_1 (C, A, B);
endmodule

// FA
module Full_adder (
  input  A,
  input  B,
  input  Cin,
  output S,
  output Cout
);

  wire half_adder_1_c, half_adder_1_s, half_adder_2_c;

  Half_adder half_adder_1 (.A(A), .B(B), .S(half_adder_1_s), .C(half_adder_1_c));
  Half_adder half_adder_2 (.A(half_adder_1_s), .B(Cin), .S(S), .C(half_adder_2_c));
  or or_1 (Cout, half_adder_2_c, half_adder_1_c);
endmodule

module _4Bit_adder (
  input  Cin,
  input  [3:0] in_2,
  input  [3:0] in_3,
  output [3:0] out_4,
  output Cout
);

  wire full_adder_1_cout, full_adder_2_cout, full_adder_3_cout;

  Full_adder full_adder_1 (.A(in_2[0]), .B(in_3[0]), .Cin(Cin), .S(out_4[0]), .Cout(full_adder_1_cout));
  Full_adder full_adder_2 (.A(in_2[1]), .B(in_3[1]), .Cin(full_adder_1_cout), .S(out_4[1]), .Cout(full_adder_2_cout));
  Full_adder full_adder_3 (.A(in_2[2]), .B(in_3[2]), .Cin(full_adder_2_cout), .S(out_4[2]), .Cout(full_adder_3_cout));
  Full_adder full_adder_4 (.A(in_2[3]), .B(in_3[3]), .Cin(full_adder_3_cout), .S(out_4[3]), .Cout(Cout));
endmodule
