// Logisim project 2013182010 김병진 Logisim(JK_Flip_Flop...4X16 Decoder).circ as structural Verilog
module JK_Flip_Flop (
  input  J,
  input  K,
  input  Ck,
  output Q,
  output Q_prime
);

  wire and_1_out, and_2_out, and_3_out, and_4_out, nand_1_out, nand_2_out, nor_1_out, nor_2_out, not_1_out;

  nand nand_1 (nand_1_out, Q, K);
  not not_1 (not_1_out, Ck);
  nand nand_2 (nand_2_out, J, Q_prime);
  and and_1 (and_1_out, nand_1_out, J, not_1_out);
  and and_2 (and_2_out, not_1_out, K, nand_2_out);
  nor nor_1 (nor_1_out, and_1_out, nor_2_out);
  nor nor_2 (nor_2_out, nor_1_out, and_2_out);
  and and_3 (and_3_out, nor_1_out, Ck);
  and and_4 (and_4_out, Ck, nor_2_out);
  nor nor_3 (Q, and_3_out, Q_prime);
  nor nor_4 (Q_prime, Q, and_4_out);
endmodule

module _4Bit_Counter (
  output [3:0] out_1
);

  wire and_1_out, and_2_out, clock_1_out;

  Clock clock_1 (.out(clock_1_out));
  T_Flip_Flop t_ff_1 (.clk(clock_1_out), .T(and_1_out), .Q(out_1[3]), .en(1'b1));  // open: Qn, preset, reset
  and and_1 (and_1_out, and_2_out, out_1[2]);
  T_Flip_Flop t_ff_2 (.clk(clock_1_out), .T(and_2_out), .Q(out_1[2]), .en(1'b1));  // open: Qn, preset, reset
  and and_2 (and_2_out, out_1[0], out_1[1]);
  T_Flip_Flop t_ff_3 (.clk(clock_1_out), .T(out_1[0]), .Q(out_1[1]), .en(1'b1));  // open: Qn, preset, reset
  T_Flip_Flop t_ff_4 (.clk(clock_1_out), .T(1'b1), .Q(out_1[0]), .en(1'b1));  // open: Qn, preset, reset
endmodule

module _3X8_Decoder (
  input  C2,
  input  C1,
  input  C0,
  input  Enable,
  output D0,
  output D1,
  output D2,
  output D3,
  output D4,
  output D5,
  output D6,
  output D7
);

  wire not_1_out, not_2_out, not_3_out;

  not not_1 (not_1_out, C2);
  not not_2 (not_2_out, C1);
  not not_3 (not_3_out, C0);
  and and_1 (D0, not_3_out, not_2_out, not_1_out, Enable);
  and and_2 (D1, C0, not_2_out, not_1_out, Enable);
  and and_3 (D2, not_3_out, C1, not_1_out, Enable);
  and and_4 (D3, C0, C1, not_1_out, Enable);
  and and_5 (D4, not_3_out, not_2_out, C2, Enable);
  and and_6 (D5, C0, not_2_out, C2, Enable);
  and and_7 (D6, not_3_out, C1, C2, Enable);
  and and_8 (D7, C0, C1, C2, Enable);
endmodule

module _3X8_Decoder____1X8_DeMux (
  input  Enable,
  input  [2:0] in_2,
  input  Enable_2,
  input  [2:0] in_4,
  output [7:0] out_5,
  output [7:0] out_6
);

  Demultiplexer #(.select(3)) demultiplexer_1 (
    .out0(out_6[0]), .out1(out_6[1]), .out2(out_6[2]), .out3(out_6[3]), .out4(out_6[4]), .out5(out_6[5]),
    .out6(out_6[6]), .out7(out_6[7]), .in(Enable_2), .sel(in_4));  // open: en
  Decoder #(.select(3)) decoder_1 (
    .out0(out_5[0]), .out1(out_5[1]), .out2(out_5[2]), .out3(out_5[3]), .out4(out_5[4]), .out5(out_5[5]),
    .out6(out_5[6]), .out7(out_5[7]), .sel(in_2), .en(Enable));
endmodule

module _4X16_Decoder (
  input  C3,
  input  C2,
  input  C1,
  input  C0,
  output [15:0] out_5
);

  wire not_1_out;

  not not_1 (not_1_out, C3);
  _3X8_Decoder u_3x8_decoder_1 (
    .C2(C2), .C1(C1), .C0(C0), .Enable(not_1_out), .D0(out_5[0]), .D1(out_5[1]), .D2(out_5[2]),
    .D3(out_5[3]), .D4(out_5[4]), .D5(out_5[5]), .D6(out_5[6]), .D7(out_5[7]));
  _3X8_Decoder u_3x8_decoder_2 (
    .C2(C2), .C1(C1), .C0(C0), .Enable(C3), .D0(out_5[8]), .D1(out_5[9]), .D2(out_5[10]), .D3(out_5[11]),
    .D4(out_5[12]), .D5(out_5[13]), .D6(out_5[14]), .D7(out_5[15]));
endmodule
