// Logisim project 2013182010 김병진 Logisim(SR Latch ... 4bit register).circ as structural Verilog
module SR_Latch (
  input  R,
  input  S,
  input  nS,
  input  nR,
  output out_5,
  output out_6,
  output out_7,
  output out_8
);

  nor nor_1 (out_5, R, out_6);
  nor nor_2 (out_6, out_5, S);
  nand nand_1 (out_7, nS, out_8);
  nand nand_2 (out_8, out_7, nR);
endmodule

module gated_SR_Latch (
  input  R,
  input  E,
  input  S,
  output Q,
  output nQ
);

  wire and_1_out, and_2_out;

  and and_1 (and_1_out, R, E);
  and and_2 (and_2_out, E, S);
  nor nor_1 (Q, and_1_out, nQ);
  nor nor_2 (nQ, Q, and_2_out);
endmodule

// D Latch
module Gated_D_Latch (
  input  Clear,
  input  D,
  input  E,
  input  Preset,
  output Q,
  output nQ
);

  wire and_1_out, and_2_out, not_1_out;

  not not_1 (not_1_out, D);
  and and_1 (and_1_out, not_1_out, E);
  and and_2 (and_2_out, E, D);
  nor nor_1 (Q, Clear, and_1_out, nQ);
  nor nor_2 (nQ, Q, and_2_out, Preset);
endmodule

// D F F
module Master_slave_edge_triggered_D_flip_flop (
  input  Clear,
  input  D,
  input  Ck,
  input  Preset,
  output Q,
  output nQ
);

  wire gated_d_latch_1_q, not_1_out;

  Gated_D_Latch gated_d_latch_1 (.Clear(1'b0), .D(D), .E(not_1_out), .Q(gated_d_latch_1_q), .Preset(1'b0));  // open: nQ
  not not_1 (not_1_out, Ck);
  Gated_D_Latch gated_d_latch_2 (.Clear(Clear), .D(gated_d_latch_1_q), .E(Ck), .Q(Q), .nQ(nQ), .Preset(Preset));
endmodule

module _4bit_register (
  input  [3:0] D,
  input  _1___Preset___0___Clear,
  input  On_off,
  input  Ck,
  output [3:0] Q
);

  wire clear_preset_pin_1_out_3, clear_preset_pin_1_out_4;

  Clear_Preset_Pin clear_preset_pin_1 (
    .preset_clear(_1___Preset___0___Clear), .out_3(clear_preset_pin_1_out_3),
    .out_4(clear_preset_pin_1_out_4), .on_off(On_off));
  Master_slave_edge_triggered_D_flip_flop master_slave_edge_triggered_d_flip_flop_1 (
    .Clear(clear_preset_pin_1_out_3), .D(D[0]), .Ck(Ck), .Q(Q[0]), .Preset(clear_preset_pin_1_out_4));  // open: nQ
  Master_slave_edge_triggered_D_flip_flop master_slave_edge_triggered_d_flip_flop_2 (
    .Clear(clear_preset_pin_1_out_3), .D(D[1]), .Ck(Ck), .Q(Q[1]), .Preset(clear_preset_pin_1_out_4));  // open: nQ
  Master_slave_edge_triggered_D_flip_flop master_slave_edge_triggered_d_flip_flop_3 (
    .Clear(clear_preset_pin_1_out_3), .D(D[2]), .Ck(Ck), .Q(Q[2]), .Preset(clear_preset_pin_1_out_4));  // open: nQ
  Master_slave_edge_triggered_D_flip_flop master_slave_edge_triggered_d_flip_flop_4 (
    .Clear(clear_preset_pin_1_out_3), .D(D[3]), .Ck(Ck), .Q(Q[3]), .Preset(clear_preset_pin_1_out_4));  // open: nQ
endmodule

// Clear/Preset
module Clear_Preset_Pin (
  input  preset_clear,
  input  on_off,
  output out_3,
  output out_4
);

  wire and_1_out, and_2_out;

  and and_1 (and_1_out, preset_clear, on_off);
  and and_2 (and_2_out, 1'b1, on_off);
  xor xor_1 (out_3, and_1_out, and_2_out);
  and and_3 (out_4, and_1_out, and_2_out);
endmodule
